// Logisim project ex3.circ as structural Verilog: 4 circuits, main circuit FSM
module FSM (
  input  FSM_Input,
  input  in_2,
  input  in_3,
  input  in_4,
  output Out1,
  output [3:0] splitter,
  output [1:0] out_7,
  output [5:0] out_8,
  output [1:0] out_9,
  output [1:0] out_10
);

  wire clock_1_out;
  wire [1:0] fsmlogic_1_next_state, register_1_q;
  wire [15:0] bit_extender_1_out;

  assign bit_extender_1_out = {{8{1'b1}}, {8{1'b1}}};  // Bit_Extender bit_extender_1
  Register #(.width(2)) register_1 (.D(fsmlogic_1_next_state), .clk(clock_1_out), .Q(register_1_q));  // open: en, clr
  Clock clock_1 (.out(clock_1_out));
  // Probe on in_2
  // Probe on in_2
  // Probe on in_3
  // Probe on bit_extender_1_out
  FSMLogic fsmlogic_1 (
    .Output(Out1), .Next_State(fsmlogic_1_next_state), .Input_Bit(FSM_Input), .Current_State(register_1_q));

  assign in_4 = in_3;
  assign out_7 = 2'b01;
  assign out_8 = 6'b111001;
  assign out_9 = 2'b10;
  assign out_10 = 2'b11;
  assign splitter = 4'b1001;

  // Other names for the same wires on the sheet: signal1 = in_2; signal2 = in_3

  // Notes on the sheet:
  //   tunnels
  //   Extenders
endmodule

// FSM Logic
module FSMLogic (
  input  Input_Bit,
  input  [1:0] Current_State,
  output Output,
  output [1:0] Next_State
);

  wire and_1_out, and_2_out, not_1_out, not_2_out, not_3_out;

  not not_1 (not_1_out, Current_State[1]);
  not not_2 (not_2_out, Input_Bit);
  not not_3 (not_3_out, Current_State[0]);
  and and_1 (and_1_out, Input_Bit, not_1_out);
  or or_1 (Output, and_1_out, and_2_out);
  and and_2 (and_2_out, not_2_out, not_3_out);
  StateBitZero statebitzero_1 (
    .New_State_0(Next_State[0]), .Input(Input_Bit), .State_Bit_0(Current_State[0]),
    .State_Bit_1(Current_State[1]));
  StateBitOne statebitone_1 (
    .New_State_1(Next_State[1]), .Input(Input_Bit), .State_Bit_0(Current_State[0]),
    .State_Bit_1(Current_State[1]));

  // Other names for the same wires on the sheet: Currrent_State_0 = Current_State[0];
  //   Current_State_1 = Current_State[1]
endmodule

// State Bit 1
module StateBitOne (
  input  Input,
  input  State_Bit_0,
  input  State_Bit_1,
  output New_State_1
);

  // NOT_Gate not_1 has open pins: in=Input, out=open
  // NOT_Gate not_2 has open pins: in=State_Bit_0, out=open
  // NOT_Gate not_3 has open pins: in=State_Bit_1, out=open
  or or_1 (New_State_1, Input, State_Bit_0);

  // Notes on the sheet:
  //   PUT CIRCUITRY HERE
endmodule

// State Bit 0
module StateBitZero (
  input  Input,
  input  State_Bit_0,
  input  State_Bit_1,
  output New_State_0
);

  wire not_1_out;

  not not_1 (not_1_out, Input);
  // NOT_Gate not_2 has open pins: in=State_Bit_0, out=open
  // NOT_Gate not_3 has open pins: in=State_Bit_1, out=open
  or or_1 (New_State_0, not_1_out, State_Bit_1);

  // Notes on the sheet:
  //   PUT CIRCUITRY HERE
endmodule
